# Fritzing sketch Trinket-Pro5v Pot RGB LED (saved by Fritzing 0.9.3b)
breadboards: 1

parts:
  Part1 = Pro Trinket 5V
  U1 = POT [package=pot_alpha_rv16af-20]
  U2 = TOUCH [package=touch2]
  C1 = Capacitor Polarized [package=cpol-radial-1000uf-63v]
  R1 = Resistor [tolerance=±5% resistance=1M package="1206 [SMD]"]
  R2 = Resistor [tolerance=±5% resistance=470 package="1206 [SMD]"]
  S2 = SWITCH-MOMENTARY-2 [package=tactile-pth-12mm]
  J1 = Power Jack [package=power_jack_smd]
  NEOPIXEL1 = Neopixel Strip -- White (60/m) [part_number=1138]
  M1 = RioRand LM2596

nets:
  GND: Part1.GND, U1.A, U2.T2, R1.Pin_1, J1.GND, M1.Pin_2
  N1: Part1.VBAT, J1.GNDBREAK, M1.Pin_1
  N2: Part1.+5V, U1.E
  N3: Part1.D4, R2.Pin_0
  N4: Part1.D12, S2.2
  N5: Part1.A0, U2.Piezo_Vibration_Sensor, R1.Pin_0
  N6: Part1.A1, U1.S
  N7: C1.+, NEOPIXEL1.+5V, M1.Pin_3
  N8: C1.-, R2.Pin_1, NEOPIXEL1.DI, NEOPIXEL1.GND, M1.Pin_4

notes:
  Adjust to 5v output
  6v-16v input

custom parts:
  Pro Trinket 5V: The Pro Trinket 5V is like an Arduino Pro Mini with more pins and USB included. Built with the common core Arduino chip, the ATmega328p, it has 18 GPIO, 2 extra analog inputs, 28K of flash, and 2K of RAM. It has onboard USB bootloading support with Optiboot support, so you can either program your Pro Trinket over USB or with a FTDI cable. The Pro Trinket is programmable using the Arduino IDE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
  TOUCH: Electrode for resistive touch detection
  Neopixel Strip -- White (60/m): Neopixel Strip, White, 60 pixels per meter.
